// Logisim project cpu.circ as structural Verilog: 11 circuits, main circuit main
module main (
  input  reset
);

  wire ALUinB, and_1_out, and_2_out, beqz, blt, clk, DMwe, inpt, isNegative, isZero, j, jal, jr,
       keyboard_1_avail, memory_latch_1_oe_latched, memory_latch_1_we_latched, nclk, or_1_out, or_2_out,
       otpt, Rdst, Rwd, Rwe;
  wire [2:0] ALUop, multiplexer_1_out, multiplexer_3_out;
  wire [3:0] opcode;
  wire [6:0] bit_extender_3_out;
  wire [7:0] keyboardOutput;
  wire [11:0] Address;
  wire [14:0] alu_3_outputdata;
  wire [15:0] alu_2_outputdata, bit_extender_1_out, bit_extender_2_out, bit_extender_4_out,
       memory_latch_1_address_latched, memory_latch_1_data_in_latched, multiplexer_2_out, multiplexer_4_out,
       multiplexer_5_out, multiplexer_6_out, multiplexer_7_out, multiplexer_8_out, multiplexer_9_out,
       myreg_1_regout, PCplusOne, ram_1_dout, rsval, rtval;

  myReg myreg_1 (.regin(multiplexer_7_out), .wEnable(nclk), .clkInput(1'b1), .reset(reset), .regout(myreg_1_regout));
  ROM #(.addrWidth(16), .dataWidth(16)) rom_1 (.addr(myreg_1_regout), .data({opcode, Address}));
  ALU alu_1 (
    .inputData2(16'h1), .outputData(PCplusOne), .inputData1(myreg_1_regout), .ALUOp(3'b000));  // open: shamt, out_6, zero
  Multiplexer #(.width(3), .enable("false")) multiplexer_1 (
    .in0(Address[8:6]), .in1(Address[5:3]), .out(multiplexer_1_out), .sel(Rdst));
  Multiplexer #(.width(16), .enable("false")) multiplexer_2 (
    .in0(multiplexer_8_out), .in1(PCplusOne), .out(multiplexer_2_out), .sel(jal));
  Multiplexer #(.width(3), .enable("false")) multiplexer_3 (
    .in0(multiplexer_1_out), .in1(3'b111), .out(multiplexer_3_out), .sel(jal));
  Keyboard keyboard_1 (.clk(clk), .re(inpt), .clr(reset), .avail(keyboard_1_avail), .data(keyboardOutput[6:0]));
  Clock clock_1 (.out(clk));
  not not_1 (keyboardOutput[7], keyboard_1_avail);
  not not_2 (nclk, clk);
  RegisterFile registerfile_1 (
    .reset(reset), .writeData(multiplexer_2_out), .clk(clk), .WE(Rwe), .writeReg(multiplexer_3_out),
    .readReg1(Address[11:9]), .readReg2(Address[8:6]), .readData1(rsval), .readData2(rtval));
  assign bit_extender_1_out = {{10{Address[5]}}, Address[5:0]};  // Bit_Extender bit_extender_1
  instructionDecoder instructiondecoder_1 (
    .opcode(opcode), .Rwe(Rwe), .Rdst(Rdst), .ALUinB(ALUinB), .ALUop(ALUop), .Rwd(Rwd), .DMwe(DMwe),
    .Blt(blt), .beqz(beqz), .otpt(otpt), .inpt(inpt), .jr(jr), .jal(jal), .j(j));
  Multiplexer #(.width(16), .enable("false")) multiplexer_4 (
    .in0(rtval), .in1(bit_extender_1_out), .out(multiplexer_4_out), .sel(ALUinB));
  // Probe on {{8{1'b0}}, keyboardOutput}
  assign bit_extender_2_out = {{10{Address[5]}}, Address[5:0]};  // Bit_Extender bit_extender_2
  Bit_Extender #(.in_width(16), .out_width(7)) bit_extender_3 (.in(rsval), .out(bit_extender_3_out));
  ALU alu_2 (
    .inputData2(bit_extender_2_out), .outputData(alu_2_outputdata), .inputData1(PCplusOne), .ALUOp(3'b000));  // open: shamt, out_6, zero
  and and_1 (and_1_out, beqz, isZero);
  and and_2 (and_2_out, blt, isNegative);
  ALU alu_3 (
    .shamt(Address[2:0]), .inputData2(multiplexer_4_out), .outputData({isNegative, alu_3_outputdata}),
    .inputData1(rsval), .ALUOp(ALUop), .zero(isZero));  // open: out_6
  TTY #(.rows(13), .cols(80)) tty_1 (.data(bit_extender_3_out), .clk(clk), .we(otpt), .clr(reset));
  or or_1 (or_1_out, and_1_out, and_2_out);
  Multiplexer #(.width(16), .enable("false")) multiplexer_5 (
    .in0(PCplusOne), .in1(alu_2_outputdata), .out(multiplexer_5_out), .sel(or_1_out));
  memory_latch memory_latch_1 (
    .address({isNegative, alu_3_outputdata}), .WE(DMwe), .clk(nclk), .data_in(rtval),
    .address_latched(memory_latch_1_address_latched), .WE_latched(memory_latch_1_we_latched),
    .OE_latched(memory_latch_1_oe_latched), .data_in_latched(memory_latch_1_data_in_latched));
  Multiplexer #(.width(16), .enable("false")) multiplexer_6 (
    .in0(multiplexer_5_out), .in1(bit_extender_4_out), .out(multiplexer_6_out), .sel(or_2_out));
  assign bit_extender_4_out = {{4{Address[11]}}, Address};  // Bit_Extender bit_extender_4
  or or_2 (or_2_out, j, jal);
  RAM #(.addrWidth(16), .dataWidth(16), .trigger("high"), .databus("bibus")) ram_1 (
    .addr(memory_latch_1_address_latched), .we(memory_latch_1_we_latched), .oe(memory_latch_1_oe_latched),
    .din(memory_latch_1_data_in_latched), .dout(ram_1_dout));
  Multiplexer #(.width(16), .enable("false")) multiplexer_7 (
    .in0(multiplexer_6_out), .in1(rsval), .out(multiplexer_7_out), .sel(jr));
  Multiplexer #(.width(16), .enable("false")) multiplexer_8 (
    .in0(multiplexer_9_out), .in1({{8{1'b0}}, keyboardOutput}), .out(multiplexer_8_out), .sel(inpt));
  Multiplexer #(.width(16), .enable("false")) multiplexer_9 (
    .in0({isNegative, alu_3_outputdata}), .in1(ram_1_dout), .out(multiplexer_9_out), .sel(Rwd));

  // Other names for the same wires on the sheet: instructionType[11:0] = Address; Rt[2:0] = Address[8:6];
  //   Rs[2:0] = Address[11:9]; Imm[5:0] = Address[5:0]; Rd[2:0] = Address[5:3]; shamt[2:0] = Address[2:0]

  // Notes on the sheet:
  //   Program Counter
endmodule

module onebitFA (
  input  Cin,
  input  B,
  input  A,
  output result,
  output cout
);

  wire and_1_out, and_2_out, xor_1_out;

  xor xor_1 (xor_1_out, B, A);
  and and_1 (and_1_out, B, A);
  xor xor_2 (result, Cin, xor_1_out);
  and and_2 (and_2_out, Cin, xor_1_out);
  or or_1 (cout, and_2_out, and_1_out);
endmodule

module myReg (
  input  [15:0] regin,
  input  wEnable,
  input  clkInput,
  input  reset,
  output [15:0] regout
);

  wire and_1_out;

  and and_1 (and_1_out, wEnable, clkInput);
  D_Flip_Flop d_ff_1 (.D(regin[0]), .clk(and_1_out), .Q(regout[0]), .reset(reset));  // open: Qn, preset
  D_Flip_Flop d_ff_2 (.D(regin[1]), .clk(and_1_out), .Q(regout[1]), .reset(reset));  // open: Qn, preset
  D_Flip_Flop d_ff_3 (.D(regin[2]), .clk(and_1_out), .Q(regout[2]), .reset(reset));  // open: Qn, preset
  D_Flip_Flop d_ff_4 (.D(regin[3]), .clk(and_1_out), .Q(regout[3]), .reset(reset));  // open: Qn, preset
  D_Flip_Flop d_ff_5 (.D(regin[4]), .clk(and_1_out), .Q(regout[4]), .reset(reset));  // open: Qn, preset
  D_Flip_Flop d_ff_6 (.D(regin[5]), .clk(and_1_out), .Q(regout[5]), .reset(reset));  // open: Qn, preset
  D_Flip_Flop d_ff_7 (.D(regin[6]), .clk(and_1_out), .Q(regout[6]), .reset(reset));  // open: Qn, preset
  D_Flip_Flop d_ff_8 (.D(regin[7]), .clk(and_1_out), .Q(regout[7]), .reset(reset));  // open: Qn, preset
  D_Flip_Flop d_ff_9 (.D(regin[8]), .clk(and_1_out), .Q(regout[8]), .reset(reset));  // open: Qn, preset
  D_Flip_Flop d_ff_10 (.D(regin[9]), .clk(and_1_out), .Q(regout[9]), .reset(reset));  // open: Qn, preset
  D_Flip_Flop d_ff_11 (.D(regin[10]), .clk(and_1_out), .Q(regout[10]), .reset(reset));  // open: Qn, preset
  D_Flip_Flop d_ff_12 (.D(regin[11]), .clk(and_1_out), .Q(regout[11]), .reset(reset));  // open: Qn, preset
  D_Flip_Flop d_ff_13 (.D(regin[12]), .clk(and_1_out), .Q(regout[12]), .reset(reset));  // open: Qn, preset
  D_Flip_Flop d_ff_14 (.D(regin[13]), .clk(and_1_out), .Q(regout[13]), .reset(reset));  // open: Qn, preset
  D_Flip_Flop d_ff_15 (.D(regin[14]), .clk(and_1_out), .Q(regout[14]), .reset(reset));  // open: Qn, preset
  D_Flip_Flop d_ff_16 (.D(regin[15]), .clk(and_1_out), .Q(regout[15]), .reset(reset));  // open: Qn, preset
endmodule

module adder_subtractor (
  input  sub,
  input  [15:0] A,
  input  [15:0] B,
  output [15:0] result,
  output beqz,
  output ovf
);

  wire onebitfa_1_cout, onebitfa_2_cout, onebitfa_3_cout, onebitfa_4_cout, onebitfa_5_cout, onebitfa_6_cout,
       onebitfa_7_cout, onebitfa_8_cout, onebitfa_9_cout, onebitfa_10_cout, onebitfa_11_cout,
       onebitfa_12_cout, onebitfa_13_cout, onebitfa_14_cout, onebitfa_15_cout, onebitfa_16_cout, xor_1_out,
       xor_2_out, xor_3_out, xor_4_out, xor_5_out, xor_6_out, xor_7_out, xor_8_out, xor_9_out, xor_10_out,
       xor_11_out, xor_12_out, xor_13_out, xor_14_out, xor_15_out, xor_16_out;

  comp comp_1 (.A(A), .B({16{1'b0}}), .isZero(beqz));
  xor xor_1 (xor_1_out, B[0], sub);
  xor xor_2 (xor_2_out, B[1], sub);
  xor xor_3 (xor_3_out, B[2], sub);
  xor xor_4 (xor_4_out, B[3], sub);
  xor xor_5 (xor_5_out, B[4], sub);
  xor xor_6 (xor_6_out, B[5], sub);
  xor xor_7 (xor_7_out, B[6], sub);
  xor xor_8 (xor_8_out, B[7], sub);
  xor xor_9 (xor_9_out, B[8], sub);
  xor xor_10 (xor_10_out, B[9], sub);
  xor xor_11 (xor_11_out, B[10], sub);
  xor xor_12 (xor_12_out, B[11], sub);
  xor xor_13 (xor_13_out, B[12], sub);
  xor xor_14 (xor_14_out, B[13], sub);
  xor xor_15 (xor_15_out, B[14], sub);
  xor xor_16 (xor_16_out, B[15], sub);
  onebitFA onebitfa_1 (.cout(onebitfa_1_cout), .result(result[0]), .A(xor_1_out), .B(A[0]), .Cin(sub));
  onebitFA onebitfa_2 (.cout(onebitfa_2_cout), .result(result[1]), .A(xor_2_out), .B(A[1]), .Cin(onebitfa_1_cout));
  onebitFA onebitfa_3 (.cout(onebitfa_3_cout), .result(result[2]), .A(xor_3_out), .B(A[2]), .Cin(onebitfa_2_cout));
  onebitFA onebitfa_4 (.cout(onebitfa_4_cout), .result(result[3]), .A(xor_4_out), .B(A[3]), .Cin(onebitfa_3_cout));
  onebitFA onebitfa_5 (.cout(onebitfa_5_cout), .result(result[4]), .A(xor_5_out), .B(A[4]), .Cin(onebitfa_4_cout));
  onebitFA onebitfa_6 (.cout(onebitfa_6_cout), .result(result[5]), .A(xor_6_out), .B(A[5]), .Cin(onebitfa_5_cout));
  onebitFA onebitfa_7 (.cout(onebitfa_7_cout), .result(result[6]), .A(xor_7_out), .B(A[6]), .Cin(onebitfa_6_cout));
  onebitFA onebitfa_8 (.cout(onebitfa_8_cout), .result(result[7]), .A(xor_8_out), .B(A[7]), .Cin(onebitfa_7_cout));
  onebitFA onebitfa_9 (.cout(onebitfa_9_cout), .result(result[8]), .A(xor_9_out), .B(A[8]), .Cin(onebitfa_8_cout));
  onebitFA onebitfa_10 (.cout(onebitfa_10_cout), .result(result[9]), .A(xor_10_out), .B(A[9]), .Cin(onebitfa_9_cout));
  onebitFA onebitfa_11 (
    .cout(onebitfa_11_cout), .result(result[10]), .A(xor_11_out), .B(A[10]), .Cin(onebitfa_10_cout));
  onebitFA onebitfa_12 (
    .cout(onebitfa_12_cout), .result(result[11]), .A(xor_12_out), .B(A[11]), .Cin(onebitfa_11_cout));
  onebitFA onebitfa_13 (
    .cout(onebitfa_13_cout), .result(result[12]), .A(xor_13_out), .B(A[12]), .Cin(onebitfa_12_cout));
  onebitFA onebitfa_14 (
    .cout(onebitfa_14_cout), .result(result[13]), .A(xor_14_out), .B(A[13]), .Cin(onebitfa_13_cout));
  onebitFA onebitfa_15 (
    .cout(onebitfa_15_cout), .result(result[14]), .A(xor_15_out), .B(A[14]), .Cin(onebitfa_14_cout));
  onebitFA onebitfa_16 (
    .cout(onebitfa_16_cout), .result(result[15]), .A(xor_16_out), .B(A[15]), .Cin(onebitfa_15_cout));
  xor xor_17 (ovf, onebitfa_15_cout, onebitfa_16_cout);
endmodule

module RegisterFile (
  input  reset,
  input  [15:0] writeData,
  input  clk,
  input  WE,
  input  [2:0] writeReg,
  input  [2:0] readReg1,
  input  [2:0] readReg2,
  output [15:0] readData1,
  output [15:0] readData2
);

  wire decoder_1_out1, decoder_1_out2, decoder_1_out3, decoder_1_out4, decoder_1_out5, decoder_1_out6,
       decoder_1_out7, decoder_2_out0, decoder_2_out1, decoder_2_out2, decoder_2_out3, decoder_2_out4,
       decoder_2_out5, decoder_2_out6, decoder_2_out7, decoder_3_out0, decoder_3_out1, decoder_3_out2,
       decoder_3_out3, decoder_3_out4, decoder_3_out5, decoder_3_out6, decoder_3_out7;
  wire [15:0] myreg_1_regout, myreg_2_regout, myreg_3_regout, myreg_4_regout, myreg_5_regout, myreg_6_regout,
       myreg_7_regout, reg0_regout;

  Decoder #(.select(3)) decoder_1 (
    .out1(decoder_1_out1), .out2(decoder_1_out2), .out3(decoder_1_out3), .out4(decoder_1_out4),
    .out5(decoder_1_out5), .out6(decoder_1_out6), .out7(decoder_1_out7), .sel(writeReg), .en(WE));  // open: out0
  // Probe on myreg_6_regout
  myReg myreg_1 (.regin(writeData), .wEnable(decoder_1_out3), .clkInput(clk), .reset(reset), .regout(myreg_1_regout));
  myReg myreg_2 (.regin(writeData), .wEnable(decoder_1_out4), .clkInput(clk), .reset(reset), .regout(myreg_2_regout));
  myReg myreg_3 (.regin(writeData), .wEnable(decoder_1_out5), .clkInput(clk), .reset(reset), .regout(myreg_3_regout));
  myReg myreg_4 (.regin(writeData), .wEnable(decoder_1_out6), .clkInput(clk), .reset(reset), .regout(myreg_4_regout));
  myReg myreg_5 (.regin(writeData), .wEnable(decoder_1_out7), .clkInput(clk), .reset(reset), .regout(myreg_5_regout));
  // Probe on reg0_regout
  myReg reg0 (.regin(writeData), .wEnable(1'b0), .clkInput(clk), .reset(reset), .regout(reg0_regout));
  myReg myreg_6 (.regin(writeData), .wEnable(decoder_1_out1), .clkInput(clk), .reset(reset), .regout(myreg_6_regout));
  // Probe on myreg_7_regout
  myReg myreg_7 (.regin(writeData), .wEnable(decoder_1_out2), .clkInput(clk), .reset(reset), .regout(myreg_7_regout));
  // Probe on myreg_1_regout
  // Probe on myreg_2_regout
  // Probe on myreg_3_regout
  assign readData1 = decoder_2_out0 ? reg0_regout : 16'bz;  // Controlled_Buffer controlled_buffer_1
  // Probe on myreg_4_regout
  // Probe on myreg_5_regout
  assign readData1 = decoder_2_out1 ? myreg_6_regout : 16'bz;  // Controlled_Buffer controlled_buffer_2
  assign readData1 = decoder_2_out2 ? myreg_7_regout : 16'bz;  // Controlled_Buffer controlled_buffer_3
  assign readData1 = decoder_2_out3 ? myreg_1_regout : 16'bz;  // Controlled_Buffer controlled_buffer_4
  assign readData1 = decoder_2_out4 ? myreg_2_regout : 16'bz;  // Controlled_Buffer controlled_buffer_5
  assign readData1 = decoder_2_out5 ? myreg_3_regout : 16'bz;  // Controlled_Buffer controlled_buffer_6
  Decoder #(.select(3)) decoder_2 (
    .out0(decoder_2_out0), .out1(decoder_2_out1), .out2(decoder_2_out2), .out3(decoder_2_out3),
    .out4(decoder_2_out4), .out5(decoder_2_out5), .out6(decoder_2_out6), .out7(decoder_2_out7), .sel(readReg1));  // open: en
  assign readData1 = decoder_2_out6 ? myreg_4_regout : 16'bz;  // Controlled_Buffer controlled_buffer_7
  assign readData1 = decoder_2_out7 ? myreg_5_regout : 16'bz;  // Controlled_Buffer controlled_buffer_8
  assign readData2 = decoder_3_out0 ? reg0_regout : 16'bz;  // Controlled_Buffer controlled_buffer_9
  assign readData2 = decoder_3_out1 ? myreg_6_regout : 16'bz;  // Controlled_Buffer controlled_buffer_10
  assign readData2 = decoder_3_out2 ? myreg_7_regout : 16'bz;  // Controlled_Buffer controlled_buffer_11
  assign readData2 = decoder_3_out3 ? myreg_1_regout : 16'bz;  // Controlled_Buffer controlled_buffer_12
  Decoder #(.select(3)) decoder_3 (
    .out0(decoder_3_out0), .out1(decoder_3_out1), .out2(decoder_3_out2), .out3(decoder_3_out3),
    .out4(decoder_3_out4), .out5(decoder_3_out5), .out6(decoder_3_out6), .out7(decoder_3_out7), .sel(readReg2));  // open: en
  assign readData2 = decoder_3_out4 ? myreg_2_regout : 16'bz;  // Controlled_Buffer controlled_buffer_13
  assign readData2 = decoder_3_out5 ? myreg_3_regout : 16'bz;  // Controlled_Buffer controlled_buffer_14
  assign readData2 = decoder_3_out6 ? myreg_4_regout : 16'bz;  // Controlled_Buffer controlled_buffer_15
  assign readData2 = decoder_3_out7 ? myreg_5_regout : 16'bz;  // Controlled_Buffer controlled_buffer_16
endmodule

module memory_latch (
  input  [15:0] address,
  input  WE,
  input  clk,
  input  [15:0] data_in,
  output [15:0] address_latched,
  output WE_latched,
  output OE_latched,
  output [15:0] data_in_latched
);

  wire DMwe_latch_q;
  wire [15:0] addr_latch_q;

  Register #(.width(16), .trigger("falling")) addr_latch (
    .D(address), .en(WE), .clk(clk), .Q(addr_latch_q));  // open: clr
  D_Flip_Flop #(.trigger("falling")) DMwe_latch (.D(WE), .clk(clk), .Q(DMwe_latch_q));  // open: Qn, preset, reset
  Register #(.width(16), .trigger("falling")) data_to_be_written (
    .D(data_in), .en(WE), .clk(clk), .Q(data_in_latched));  // open: clr
  Multiplexer #(.width(16), .enable("false")) multiplexer_1 (
    .in0(address), .in1(addr_latch_q), .out(address_latched), .sel(DMwe_latch_q));
  and and_1 (WE_latched, clk, DMwe_latch_q);
  not not_1 (OE_latched, WE_latched);
endmodule

module shiftCircuitLeft (
  input  [15:0] inputData,
  input  [2:0] shamt,
  output [15:0] result
);

  wire multiplexer_1_out, multiplexer_2_out, multiplexer_3_out, multiplexer_4_out, multiplexer_5_out,
       multiplexer_6_out, multiplexer_7_out, multiplexer_8_out, multiplexer_9_out, multiplexer_10_out,
       multiplexer_11_out, multiplexer_12_out, multiplexer_13_out, multiplexer_14_out, multiplexer_15_out,
       multiplexer_16_out, multiplexer_17_out, multiplexer_18_out, multiplexer_19_out, multiplexer_20_out,
       multiplexer_21_out, multiplexer_22_out, multiplexer_23_out, multiplexer_24_out, multiplexer_25_out,
       multiplexer_26_out, multiplexer_27_out, multiplexer_28_out, multiplexer_29_out, multiplexer_30_out,
       multiplexer_31_out, multiplexer_32_out;

  Multiplexer #(.enable("false")) multiplexer_1 (
    .in0(inputData[15]), .in1(inputData[11]), .out(multiplexer_1_out), .sel(shamt[2]));
  Multiplexer #(.enable("false")) multiplexer_2 (
    .in0(inputData[14]), .in1(inputData[10]), .out(multiplexer_2_out), .sel(shamt[2]));
  Multiplexer #(.enable("false")) multiplexer_3 (
    .in0(inputData[13]), .in1(inputData[9]), .out(multiplexer_3_out), .sel(shamt[2]));
  Multiplexer #(.enable("false")) multiplexer_4 (
    .in0(inputData[12]), .in1(inputData[8]), .out(multiplexer_4_out), .sel(shamt[2]));
  Multiplexer #(.enable("false")) multiplexer_5 (
    .in0(inputData[11]), .in1(inputData[7]), .out(multiplexer_5_out), .sel(shamt[2]));
  Multiplexer #(.enable("false")) multiplexer_6 (
    .in0(inputData[10]), .in1(inputData[6]), .out(multiplexer_6_out), .sel(shamt[2]));
  Multiplexer #(.enable("false")) multiplexer_7 (
    .in0(inputData[9]), .in1(inputData[5]), .out(multiplexer_7_out), .sel(shamt[2]));
  Multiplexer #(.enable("false")) multiplexer_8 (
    .in0(inputData[8]), .in1(inputData[4]), .out(multiplexer_8_out), .sel(shamt[2]));
  Multiplexer #(.enable("false")) multiplexer_9 (
    .in0(inputData[7]), .in1(inputData[3]), .out(multiplexer_9_out), .sel(shamt[2]));
  Multiplexer #(.enable("false")) multiplexer_10 (
    .in0(inputData[6]), .in1(inputData[2]), .out(multiplexer_10_out), .sel(shamt[2]));
  Multiplexer #(.enable("false")) multiplexer_11 (
    .in0(inputData[5]), .in1(inputData[1]), .out(multiplexer_11_out), .sel(shamt[2]));
  Multiplexer #(.enable("false")) multiplexer_12 (
    .in0(inputData[4]), .in1(inputData[0]), .out(multiplexer_12_out), .sel(shamt[2]));
  Multiplexer #(.enable("false")) multiplexer_13 (
    .in0(inputData[3]), .in1(1'b0), .out(multiplexer_13_out), .sel(shamt[2]));
  Multiplexer #(.enable("false")) multiplexer_14 (
    .in0(inputData[2]), .in1(1'b0), .out(multiplexer_14_out), .sel(shamt[2]));
  Multiplexer #(.enable("false")) multiplexer_15 (
    .in0(inputData[1]), .in1(1'b0), .out(multiplexer_15_out), .sel(shamt[2]));
  Multiplexer #(.enable("false")) multiplexer_16 (
    .in0(inputData[0]), .in1(1'b0), .out(multiplexer_16_out), .sel(shamt[2]));
  Multiplexer #(.enable("false")) multiplexer_17 (
    .in0(multiplexer_1_out), .in1(multiplexer_3_out), .out(multiplexer_17_out), .sel(shamt[1]));
  Multiplexer #(.enable("false")) multiplexer_18 (
    .in0(multiplexer_2_out), .in1(multiplexer_4_out), .out(multiplexer_18_out), .sel(shamt[1]));
  Multiplexer #(.enable("false")) multiplexer_19 (
    .in0(multiplexer_3_out), .in1(multiplexer_5_out), .out(multiplexer_19_out), .sel(shamt[1]));
  Multiplexer #(.enable("false")) multiplexer_20 (
    .in0(multiplexer_4_out), .in1(multiplexer_6_out), .out(multiplexer_20_out), .sel(shamt[1]));
  Multiplexer #(.enable("false")) multiplexer_21 (
    .in0(multiplexer_5_out), .in1(multiplexer_7_out), .out(multiplexer_21_out), .sel(shamt[1]));
  Multiplexer #(.enable("false")) multiplexer_22 (
    .in0(multiplexer_6_out), .in1(multiplexer_8_out), .out(multiplexer_22_out), .sel(shamt[1]));
  Multiplexer #(.enable("false")) multiplexer_23 (
    .in0(multiplexer_7_out), .in1(multiplexer_9_out), .out(multiplexer_23_out), .sel(shamt[1]));
  Multiplexer #(.enable("false")) multiplexer_24 (
    .in0(multiplexer_8_out), .in1(multiplexer_10_out), .out(multiplexer_24_out), .sel(shamt[1]));
  Multiplexer #(.enable("false")) multiplexer_25 (
    .in0(multiplexer_9_out), .in1(multiplexer_11_out), .out(multiplexer_25_out), .sel(shamt[1]));
  Multiplexer #(.enable("false")) multiplexer_26 (
    .in0(multiplexer_10_out), .in1(multiplexer_12_out), .out(multiplexer_26_out), .sel(shamt[1]));
  Multiplexer #(.enable("false")) multiplexer_27 (
    .in0(multiplexer_11_out), .in1(multiplexer_13_out), .out(multiplexer_27_out), .sel(shamt[1]));
  Multiplexer #(.enable("false")) multiplexer_28 (
    .in0(multiplexer_12_out), .in1(multiplexer_14_out), .out(multiplexer_28_out), .sel(shamt[1]));
  Multiplexer #(.enable("false")) multiplexer_29 (
    .in0(multiplexer_13_out), .in1(multiplexer_15_out), .out(multiplexer_29_out), .sel(shamt[1]));
  Multiplexer #(.enable("false")) multiplexer_30 (
    .in0(multiplexer_14_out), .in1(multiplexer_16_out), .out(multiplexer_30_out), .sel(shamt[1]));
  Multiplexer #(.enable("false")) multiplexer_31 (
    .in0(multiplexer_15_out), .in1(1'b0), .out(multiplexer_31_out), .sel(shamt[1]));
  Multiplexer #(.enable("false")) multiplexer_32 (
    .in0(multiplexer_16_out), .in1(1'b0), .out(multiplexer_32_out), .sel(shamt[1]));
  Multiplexer #(.enable("false")) multiplexer_33 (
    .in0(multiplexer_17_out), .in1(multiplexer_18_out), .out(result[15]), .sel(shamt[0]));
  Multiplexer #(.enable("false")) multiplexer_34 (
    .in0(multiplexer_18_out), .in1(multiplexer_19_out), .out(result[14]), .sel(shamt[0]));
  Multiplexer #(.enable("false")) multiplexer_35 (
    .in0(multiplexer_19_out), .in1(multiplexer_20_out), .out(result[13]), .sel(shamt[0]));
  Multiplexer #(.enable("false")) multiplexer_36 (
    .in0(multiplexer_20_out), .in1(multiplexer_21_out), .out(result[12]), .sel(shamt[0]));
  Multiplexer #(.enable("false")) multiplexer_37 (
    .in0(multiplexer_21_out), .in1(multiplexer_22_out), .out(result[11]), .sel(shamt[0]));
  Multiplexer #(.enable("false")) multiplexer_38 (
    .in0(multiplexer_22_out), .in1(multiplexer_23_out), .out(result[10]), .sel(shamt[0]));
  Multiplexer #(.enable("false")) multiplexer_39 (
    .in0(multiplexer_23_out), .in1(multiplexer_24_out), .out(result[9]), .sel(shamt[0]));
  Multiplexer #(.enable("false")) multiplexer_40 (
    .in0(multiplexer_24_out), .in1(multiplexer_25_out), .out(result[8]), .sel(shamt[0]));
  Multiplexer #(.enable("false")) multiplexer_41 (
    .in0(multiplexer_25_out), .in1(multiplexer_26_out), .out(result[7]), .sel(shamt[0]));
  Multiplexer #(.enable("false")) multiplexer_42 (
    .in0(multiplexer_26_out), .in1(multiplexer_27_out), .out(result[6]), .sel(shamt[0]));
  Multiplexer #(.enable("false")) multiplexer_43 (
    .in0(multiplexer_27_out), .in1(multiplexer_28_out), .out(result[5]), .sel(shamt[0]));
  Multiplexer #(.enable("false")) multiplexer_44 (
    .in0(multiplexer_28_out), .in1(multiplexer_29_out), .out(result[4]), .sel(shamt[0]));
  Multiplexer #(.enable("false")) multiplexer_45 (
    .in0(multiplexer_29_out), .in1(multiplexer_30_out), .out(result[3]), .sel(shamt[0]));
  Multiplexer #(.enable("false")) multiplexer_46 (
    .in0(multiplexer_30_out), .in1(multiplexer_31_out), .out(result[2]), .sel(shamt[0]));
  Multiplexer #(.enable("false")) multiplexer_47 (
    .in0(multiplexer_31_out), .in1(multiplexer_32_out), .out(result[1]), .sel(shamt[0]));
  Multiplexer #(.enable("false")) multiplexer_48 (
    .in0(multiplexer_32_out), .in1(1'b0), .out(result[0]), .sel(shamt[0]));

  // Other names for the same wires on the sheet: bit0 = inputData[0]; bit1 = inputData[1]; bit2 = inputData[2];
  //   bit3 = inputData[3]; bit4 = inputData[4]; bit5 = inputData[5]; bit6 = inputData[6]; bit7 = inputData[7];
  //   bit8 = inputData[8]; bit9 = inputData[9]; bit10 = inputData[10]; bit11 = inputData[11]; bit12 = inputData[12];
  //   bit13 = inputData[13]; bit14 = inputData[14]; bit15 = inputData[15]; out0 = result[0]; out1 = result[1];
  //   out2 = result[2]; out3 = result[3]; out4 = result[4]; out5 = result[5]; out6 = result[6]; out7 = result[7];
  //   out8 = result[8]; out9 = result[9]; out10 = result[10]; out11 = result[11]; out12 = result[12];
  //   out13 = result[13]; out14 = result[14]; out15 = result[15]; s0 = shamt[0]; s1 = shamt[1]; s2 = shamt[2]
endmodule

module shiftCircuitRight (
  input  [15:0] inpt,
  input  [2:0] shamt,
  output [15:0] result
);

  shiftCircuitLeft shiftcircuitleft_1 (
    .inputData({inpt[0], inpt[1], inpt[2], inpt[3], inpt[4], inpt[5], inpt[6], inpt[7], inpt[8], inpt[9], inpt[10], inpt[11], inpt[12], inpt[13], inpt[14], inpt[15]}),
    .shamt(shamt),
    .result({result[0], result[1], result[2], result[3], result[4], result[5], result[6], result[7], result[8], result[9], result[10], result[11], result[12], result[13], result[14], result[15]}));
endmodule

module ALU (
  input  [15:0] inputData1,
  input  [15:0] inputData2,
  input  [2:0] ALUOp,
  input  [2:0] shamt,
  output [15:0] outputData,
  output out_6,
  output zero
);

  wire add, InNot, InXor, shiftLeft, shiftRight, sub;
  wire [15:0] addsubOut, OutNot, outShiftLeftLogical, outShiftRightLogical, OutXor;

  assign OutNot = ~inputData1;  // NOT_Gate not_1, 16 bits wide
  assign OutXor = inputData1 ^ inputData2;  // XOR_Gate xor_1, 16 bits wide
  Decoder #(.select(3), .enable("false")) decoder_1 (
    .out0(add), .out1(sub), .out2(InNot), .out3(InXor), .out4(shiftLeft), .out5(shiftRight), .sel(ALUOp));  // open: out6, out7
  adder_subtractor adder_subtractor_1 (
    .ovf(out_6), .B(inputData2), .sub(sub), .A(inputData1), .result(addsubOut), .beqz(zero));
  shiftCircuitLeft shiftcircuitleft_1 (.inputData(inputData1), .shamt(shamt), .result(outShiftLeftLogical));
  shiftCircuitRight shiftcircuitright_1 (.inpt(inputData1), .shamt(shamt), .result(outShiftRightLogical));
  Multiplexer #(.select(3), .width(16), .enable("false")) multiplexer_1 (
    .in0(addsubOut), .in1(addsubOut), .in2(OutNot), .in3(OutXor), .in4(outShiftLeftLogical),
    .in5(outShiftRightLogical), .out(outputData), .sel(ALUOp));  // open: in6, in7

  // Other names for the same wires on the sheet: In1[15:0] = inputData1; In2[15:0] = inputData2;
  //   Out[15:0] = outputData

  // Notes on the sheet:
  //   Xor
  //   Not
  //   Add Subtract
  //   SLL
  //   SRL
endmodule

module instructionDecoder (
  input  [3:0] opcode,
  output Rwe,
  output Rdst,
  output ALUinB,
  output [2:0] ALUop,
  output Rwd,
  output DMwe,
  output Blt,
  output beqz,
  output otpt,
  output inpt,
  output jr,
  output jal,
  output j
);

  wire add, addi, nott, shll, shrl, sub, Xorr;

  Decoder #(.select(4), .enable("false")) decoder_1 (
    .out0(add), .out1(sub), .out2(addi), .out3(nott), .out4(Xorr), .out5(shll), .out6(shrl), .out7(Rwd),
    .out8(DMwe), .out9(beqz), .out10(Blt), .out11(j), .out12(jr), .out13(jal), .out14(inpt), .out15(otpt),
    .sel(opcode));
  or or_1 (ALUop[2], shrl, shll);
  or or_2 (Rwe, nott, add, sub, addi, shrl, jal, shll, Rwd, inpt, Xorr);
  or or_3 (ALUop[1], nott, Xorr);
  or or_4 (ALUop[0], shrl, sub, Xorr, Blt);
  or or_5 (Rdst, nott, Xorr, add, sub, shrl, shll, inpt);
  or or_6 (ALUinB, Rwd, addi, DMwe);

  // Other names for the same wires on the sheet: inputt = inpt; lw = Rwd; outputt = otpt; sw = DMwe
endmodule

module comp (
  input  [15:0] A,
  input  [15:0] B,
  output isZero
);

  wire and_1_out, and_2_out, and_3_out, and_4_out, xnor_1_out, xnor_2_out, xnor_3_out, xnor_4_out,
       xnor_5_out, xnor_6_out, xnor_7_out, xnor_8_out, xnor_9_out, xnor_10_out, xnor_11_out, xnor_12_out,
       xnor_13_out, xnor_14_out, xnor_15_out, xnor_16_out;

  xnor xnor_1 (xnor_1_out, A[0], B[0]);
  xnor xnor_2 (xnor_2_out, A[1], B[1]);
  xnor xnor_3 (xnor_3_out, A[2], B[2]);
  xnor xnor_4 (xnor_4_out, A[3], B[3]);
  xnor xnor_5 (xnor_5_out, A[4], B[4]);
  xnor xnor_6 (xnor_6_out, A[5], B[5]);
  xnor xnor_7 (xnor_7_out, A[6], B[6]);
  xnor xnor_8 (xnor_8_out, A[7], B[7]);
  xnor xnor_9 (xnor_9_out, A[8], B[8]);
  xnor xnor_10 (xnor_10_out, A[9], B[9]);
  xnor xnor_11 (xnor_11_out, A[10], B[10]);
  xnor xnor_12 (xnor_12_out, A[11], B[11]);
  xnor xnor_13 (xnor_13_out, A[12], B[12]);
  xnor xnor_14 (xnor_14_out, A[13], B[13]);
  xnor xnor_15 (xnor_15_out, A[14], B[14]);
  xnor xnor_16 (xnor_16_out, A[15], B[15]);
  and and_1 (and_1_out, xnor_1_out, xnor_2_out, xnor_3_out, xnor_4_out);
  and and_2 (and_2_out, xnor_5_out, xnor_6_out, xnor_7_out, xnor_8_out);
  and and_3 (and_3_out, xnor_9_out, xnor_10_out, xnor_11_out, xnor_12_out);
  and and_4 (and_4_out, xnor_13_out, xnor_14_out, xnor_15_out, xnor_16_out);
  and and_5 (isZero, and_1_out, and_2_out, and_3_out, and_4_out);
endmodule
